# Fritzing sketch DSP Activity #3 Mapper (saved by Fritzing 0.9.0b)
breadboards: 1

parts:
  Part1 = SRF05 Ultrasonic Rangefinder
  Part2 = Arduino Uno (Rev3)
  LCD1 = LCD screen
  R1 = Trimmer Potentiometer [maximum_resistance=10kΩ package=THT]
  J1 = Basic Servo
  J2 = Basic Servo

nets:
  VCC: Part1.VCC, R1.leg2, J1.vcc, J2.vcc
  N1: Part1.Trig, Part2.D13/SCK
  N2: Part1.Echo, Part2.D12/MISO
  GND: Part1.GND, R1.leg1, J1.gnd, J2.gnd
  N3: Part2.D8, J2.pulse
  N4: Part2.D9_PWM, J1.pulse
  GND_2: Part2.GND, LCD1.VSS, LCD1.R/W
  N5: Part2.D2, LCD1.DB4
  N6: Part2.D3_PWM, LCD1.DB5
  N7: Part2.D4, LCD1.DB6
  N8: Part2.D5_PWM, LCD1.DB7
  N9: Part2.D6_PWM, LCD1.E
  N10: Part2.D7, LCD1.RS
  5V: Part2.5V, LCD1.VDD
  N11: LCD1.V0, R1.wiper
