# Fritzing sketch DSP Activity #3 (saved by Fritzing 0.9.0b)
breadboards: 1

parts:
  Part1 = SRF05 Ultrasonic Rangefinder
  Part2 = Arduino Uno (Rev3)
  LCD1 = LCD screen
  R1 = Trimmer Potentiometer [maximum_resistance=10kΩ package=THT]

nets:
  N1: Part1.VCC, R1.leg2
  N2: Part1.Trig, Part2.D13/SCK
  N3: Part1.Echo, Part2.D12/MISO
  N4: Part1.GND, R1.leg1
  GND: Part2.GND, LCD1.VSS, LCD1.R/W
  N5: Part2.D2, LCD1.DB4
  N6: Part2.D3_PWM, LCD1.DB5
  N7: Part2.D4, LCD1.DB6
  N8: Part2.D5_PWM, LCD1.DB7
  N9: Part2.D6_PWM, LCD1.E
  N10: Part2.D7, LCD1.RS
  5V: Part2.5V, LCD1.VDD
  N11: LCD1.V0, R1.wiper
